# Fritzing sketch Fritzing (saved by Fritzing 0.9.3b)
breadboards: 1

parts:
  U2 = ESP8266 WiFi Module [part_number=ESP8266]
  R1 = Resistor [tolerance=±5% resistance=10k package="0402 [SMD]"]
  U3 = V_REG_LD1117VXX [package=78xxl]
  C1 = Capacitor Polarized [package=cpol-radial-10uf-25v]
  C2 = Capacitor Polarized [package=cpol-radial-10uf-25v]
  R3 = Resistor [tolerance=±5% resistance=470 package="0805 [SMD]"]
  LED1 = LED - 3mm [color="Red (633nm)" package="3 mm [THT]"]
  V1 = DC Power [voltage=5]
  KY-1 = Keyes Relay [package=THT]
  LED2 = LEDs [package=led10mm]
  R2 = Resistor [tolerance=±5% resistance=10k package="0402 [SMD]"]

nets (from the schematic view):
  N1: U2.VCC, R1.Pin_0, U3.OUT, C1.+, R2.Pin_0
  N2: U2.GPIO_2, R1.Pin_1, KY-1.signal
  N3: U2.CH_PD, R2.Pin_1
  GND: U2.GND, U3.GND, C1.-, C2.-, LED1.cathode, V1.V-, KY-1.ground
  N4: U3.IN, C2.+, R3.Pin_0, V1.V+, KY-1.power
  N5: R3.Pin_1, LED1.anode
  N6: KY-1.C, LED2.A
  N7: KY-1.NO, LED2.C

custom parts:
  ESP8266 WiFi Module: Generic WiFi Module based on the ESP8266 with onboard PCB antenna and UART communications
  Keyes Relay: The Keyes 5V relay module is suitable for SCM development, home appliance control. It uses a 5V~12V TIL control signal which can control DC / AC signal.
  LEDs: LEDs Standard schematic elements and footprints for 5mm, 3mm, 1206, and 0603 sized LEDs. 5mm - Spark Fun Electronics SKU : COM-00529 (and others)
